// Logisim project ControlUnit.circ as structural Verilog: 1 circuit, main circuit main
module main (
  input  start,
  input  win,
  input  lose,
  input  clock,
  output L1,
  output L2,
  output L3,
  output L4,
  output L5,
  output L6,
  output L7,
  output L8,
  output Reset,
  output Letter,
  output Compare,
  output Rlet
);

  wire and_1_out, and_2_out, and_7_out, and_8_out, and_9_out, and_10_out, not_1_out, not_2_out, not_3_out,
       not_4_out, not_5_out, not_6_out, not_7_out, not_8_out, not_9_out, not_10_out, not_11_out, not_12_out,
       not_13_out, not_14_out, not_15_out, not_16_out, not_17_out, not_18_out, or_1_out, or_2_out, xor_1_out;
  wire [2:0] n0_out, STATE_q;

  not not_1 (not_1_out, win);
  and and_1 (and_1_out, not_1_out, lose);
  not not_2 (not_2_out, STATE_q[1]);
  Register #(.width(3)) STATE (.D(n0_out), .en(1'b1), .Q(STATE_q), .clk(clock));  // open: clr
  or or_1 (or_1_out, and_1_out, win);
  not not_3 (not_3_out, STATE_q[2]);
  xor xor_1 (xor_1_out, STATE_q[1], STATE_q[0]);
  not not_4 (not_4_out, STATE_q[1]);
  not not_5 (not_5_out, STATE_q[0]);
  not not_6 (not_6_out, win);
  not not_7 (not_7_out, lose);
  and and_2 (and_2_out, not_2_out, start);
  or or_2 (or_2_out, and_2_out, STATE_q[1]);
  not not_8 (not_8_out, STATE_q[2]);
  and and_3 (L1, not_8_out, not_9_out, STATE_q[0]);
  not not_9 (not_9_out, STATE_q[1]);
  not not_10 (not_10_out, STATE_q[2]);
  and and_4 (Letter, not_10_out, STATE_q[1], not_11_out);
  not not_11 (not_11_out, STATE_q[0]);
  not not_12 (not_12_out, STATE_q[2]);
  and and_5 (Compare, not_12_out, STATE_q[1], STATE_q[0]);
  and and_6 (Rlet, STATE_q[2], not_13_out, not_14_out);
  not not_13 (not_13_out, STATE_q[1]);
  not not_14 (not_14_out, STATE_q[0]);
  not not_15 (not_15_out, STATE_q[1]);
  and and_7 (and_7_out, STATE_q[2], not_15_out, not_16_out, or_1_out);
  not not_16 (not_16_out, STATE_q[0]);
  and and_8 (and_8_out, not_3_out, xor_1_out);
  and and_9 (and_9_out, STATE_q[2], not_4_out, not_5_out, not_6_out, not_7_out);
  not not_17 (not_17_out, STATE_q[2]);
  not not_18 (not_18_out, STATE_q[0]);
  and and_10 (and_10_out, not_17_out, not_18_out, or_2_out);
  or n2 (n0_out[2], Compare, and_7_out);
  or n1 (n0_out[1], and_8_out, and_9_out);
  or n0 (n0_out[0], and_10_out, and_7_out);

  assign L2 = L1;
  assign L3 = L1;
  assign L4 = L1;
  assign L5 = L1;
  assign L6 = L1;
  assign L7 = L1;
  assign L8 = L1;
  assign Reset = L1;
endmodule
