// Logisim project Hangman.circ as structural Verilog: 1 circuit, main circuit main
module main (
  input  [7:0] _1_letter,
  input  [7:0] _2_letter,
  input  [7:0] _3_letter,
  input  [7:0] _4_letter,
  input  [7:0] _5_letter,
  input  [7:0] _6_letter,
  input  [7:0] _7_letter,
  input  [7:0] _8_letter
);

  wire a_out, b_out, c_out, clk_out, clock_1_out, clock_2_out, ControlUnit_compare, ControlUnit_l1,
       ControlUnit_l2, ControlUnit_l3, ControlUnit_l4, ControlUnit_l5, ControlUnit_l6, ControlUnit_l7,
       ControlUnit_l8, ControlUnit_letter, ControlUnit_reset, ControlUnit_rlet, d_out, Datapath_lose,
       Datapath_win, e_out, f_out, g_out, h_out, i_out, j_out, k_out, l_out, m_out, main_1_a, main_1_b,
       main_1_c, main_1_d, main_1_e, main_1_f, main_1_g, main_2_a, main_2_b, main_2_c, main_2_d, main_2_e,
       main_2_f, main_2_g, main_3_a, main_3_b, main_3_c, main_3_d, main_3_e, main_3_f, main_3_g, n_out,
       o_out, p_out, q_out, r_out, Reset_Scores_out, s_out, start_out, t_out, u_out, v_out, w_out, x_out,
       y_out, z_out;
  wire [3:0] Datapath_counter, LetterCounter_letternumber, ScoreBoard_computer, ScoreBoard_player;
  wire [6:0] ledMatrix_c1, ledMatrix_c2, ledMatrix_c3, ledMatrix_c4, ledMatrix_c5, printTTY_print;
  wire [7:0] Datapath__1_letter_2, Datapath__2_letter_2, Datapath__3_letter_2, Datapath__4_letter_2,
       Datapath__5_letter_2, Datapath__6_letter_2, Datapath__7_letter_2, Datapath__8_letter_2,
       multiplexer_1_out, multiplexer_2_out, multiplexer_3_out, multiplexer_4_out, multiplexer_5_out,
       multiplexer_6_out, multiplexer_7_out, multiplexer_8_out;

  Clock #(.highDuration(2), .lowDuration(2)) clk (.out(clk_out));
  Clock clock_1 (.out(clock_1_out));
  ControlUnit_main ControlUnit (
    .start(start_out), .win(Datapath_win), .lose(Datapath_lose), .clock(clk_out), .L1(ControlUnit_l1),
    .L2(ControlUnit_l2), .L3(ControlUnit_l3), .L4(ControlUnit_l4), .L5(ControlUnit_l5), .L6(ControlUnit_l6),
    .L7(ControlUnit_l7), .L8(ControlUnit_l8), .Reset(ControlUnit_reset), .Letter(ControlUnit_letter),
    .Compare(ControlUnit_compare), .Rlet(ControlUnit_rlet));
  Button start (.out(start_out));
  Button a (.out(a_out));
  Button b (.out(b_out));
  Button c (.out(c_out));
  Button d (.out(d_out));
  Button e (.out(e_out));
  Button f (.out(f_out));
  Button g (.out(g_out));
  Button h (.out(h_out));
  Button i (.out(i_out));
  Button j (.out(j_out));
  Button k (.out(k_out));
  Button l (.out(l_out));
  Button m (.out(m_out));
  Button n (.out(n_out));
  Button o (.out(o_out));
  Button p (.out(p_out));
  Button q (.out(q_out));
  Button r (.out(r_out));
  Button s (.out(s_out));
  Button t (.out(t_out));
  Button u (.out(u_out));
  Button v (.out(v_out));
  Button w (.out(w_out));
  Button x (.out(x_out));
  Button y (.out(y_out));
  Button z (.out(z_out));
  LetterCounter_main LetterCounter (
    ._1_letter(_1_letter), ._2_letter(_2_letter), ._3_letter(_3_letter), ._4_letter(_4_letter),
    ._5_letter(_5_letter), ._6_letter(_6_letter), ._7_letter(_7_letter), ._8_letter(_8_letter),
    .start(start_out), .clock(clock_1_out), .letterNumber(LetterCounter_letternumber));
  datapath_main Datapath (
    ._1_letter(_1_letter), .L1(ControlUnit_l1), ._2_letter(_2_letter), .L2(ControlUnit_l2),
    ._3_letter(_3_letter), .L3(ControlUnit_l3), ._4_letter(_4_letter), .L4(ControlUnit_l4),
    ._5_letter(_5_letter), .L5(ControlUnit_l5), ._6_letter(_6_letter), .L6(ControlUnit_l6),
    ._7_letter(_7_letter), .L7(ControlUnit_l7), ._8_letter(_8_letter), .L8(ControlUnit_l8), .a(a_out),
    .b(b_out), .c(c_out), .d(d_out), .e(e_out), .f(f_out), .g(g_out), .h(h_out), .i(i_out), .j(j_out),
    .k(k_out), .l(l_out), .m(m_out), .n(n_out), .o(o_out), .p(p_out), .q(q_out), .r(r_out), .s(s_out),
    .t(t_out), .u(u_out), .v(v_out), .w(w_out), .x(x_out), .y(y_out), .z(z_out), .Reset(ControlUnit_reset),
    .letter(ControlUnit_letter), .comp(ControlUnit_compare), .Rlet(ControlUnit_rlet), .Clock(clk_out),
    .Start(start_out), ._1_letter_2(Datapath__1_letter_2), ._2_letter_2(Datapath__2_letter_2),
    ._3_letter_2(Datapath__3_letter_2), ._4_letter_2(Datapath__4_letter_2),
    ._5_letter_2(Datapath__5_letter_2), ._6_letter_2(Datapath__6_letter_2),
    ._7_letter_2(Datapath__7_letter_2), ._8_letter_2(Datapath__8_letter_2), .win(Datapath_win),
    .lose(Datapath_lose), .counter(Datapath_counter));
  Multiplexer #(.width(8), .enable("false")) multiplexer_1 (
    .in0(Datapath__1_letter_2), .in1(_1_letter), .out(multiplexer_1_out), .sel(Datapath_lose));
  Multiplexer #(.width(8), .enable("false")) multiplexer_2 (
    .in0(Datapath__2_letter_2), .in1(_2_letter), .out(multiplexer_2_out), .sel(Datapath_lose));
  Multiplexer #(.width(8), .enable("false")) multiplexer_3 (
    .in0(Datapath__3_letter_2), .in1(_3_letter), .out(multiplexer_3_out), .sel(Datapath_lose));
  Multiplexer #(.width(8), .enable("false")) multiplexer_4 (
    .in0(Datapath__4_letter_2), .in1(_4_letter), .out(multiplexer_4_out), .sel(Datapath_lose));
  Multiplexer #(.width(8), .enable("false")) multiplexer_5 (
    .in0(Datapath__5_letter_2), .in1(_5_letter), .out(multiplexer_5_out), .sel(Datapath_lose));
  Multiplexer #(.width(8), .enable("false")) multiplexer_6 (
    .in0(Datapath__6_letter_2), .in1(_6_letter), .out(multiplexer_6_out), .sel(Datapath_lose));
  Multiplexer #(.width(8), .enable("false")) multiplexer_7 (
    .in0(Datapath__7_letter_2), .in1(_7_letter), .out(multiplexer_7_out), .sel(Datapath_lose));
  Multiplexer #(.width(8), .enable("false")) multiplexer_8 (
    .in0(Datapath__8_letter_2), .in1(_8_letter), .out(multiplexer_8_out), .sel(Datapath_lose));
  Decoder_main main_1 (
    .number(LetterCounter_letternumber), .a(main_1_a), .b(main_1_b), .c(main_1_c), .d(main_1_d),
    .e(main_1_e), .f(main_1_f), .g(main_1_g));
  DotMatrix dotmatrix_1 (
    .col0(ledMatrix_c1), .col1(ledMatrix_c2), .col2(ledMatrix_c3), .col3(ledMatrix_c4), .col4(ledMatrix_c5));
  ledMatrix_main ledMatrix (
    .counter(Datapath_counter), .c1(ledMatrix_c1), .c2(ledMatrix_c2), .c3(ledMatrix_c3), .c4(ledMatrix_c4),
    .c5(ledMatrix_c5));
  _7_Segment_Display u_7_segment_display_1 (
    .g(main_1_g), .f(main_1_f), .a(main_1_a), .b(main_1_b), .e(main_1_e), .d(main_1_d), .c(main_1_c),
    .dp(1'b0));
  Clock clock_2 (.out(clock_2_out));
  printTTY_main printTTY (
    ._1_letter(multiplexer_1_out), ._2_letter(multiplexer_2_out), ._3_letter(multiplexer_3_out),
    ._4_letter(multiplexer_4_out), ._5_letter(multiplexer_5_out), ._6_letter(multiplexer_6_out),
    ._7_letter(multiplexer_7_out), ._8_letter(multiplexer_8_out), .reset(start_out), .clk(clock_2_out),
    .print(printTTY_print));
  TTY #(.rows(11), .cols(64)) tty_1 (.data(printTTY_print), .clk(clock_2_out), .clr(start_out));  // open: we
  Decoder_main main_2 (
    .number(ScoreBoard_player), .a(main_2_a), .b(main_2_b), .c(main_2_c), .d(main_2_d), .e(main_2_e),
    .f(main_2_f), .g(main_2_g));
  Button Reset_Scores (.out(Reset_Scores_out));
  scoreBoard_main ScoreBoard (
    .win(Datapath_win), .Reset(Reset_Scores_out), .lose(Datapath_lose), .player(ScoreBoard_player),
    .computer(ScoreBoard_computer));
  _7_Segment_Display u_7_segment_display_2 (
    .g(main_2_g), .f(main_2_f), .a(main_2_a), .b(main_2_b), .e(main_2_e), .d(main_2_d), .c(main_2_c),
    .dp(1'b0));
  Decoder_main main_3 (
    .number(ScoreBoard_computer), .a(main_3_a), .b(main_3_b), .c(main_3_c), .d(main_3_d), .e(main_3_e),
    .f(main_3_f), .g(main_3_g));
  _7_Segment_Display u_7_segment_display_3 (
    .g(main_3_g), .f(main_3_f), .a(main_3_a), .b(main_3_b), .e(main_3_e), .d(main_3_d), .c(main_3_c),
    .dp(1'b0));

  // Notes on the sheet:
  //   Number of characters in word
  //   Hangman
  //   ScoreBoard
endmodule
