// Logisim project LetterCounter.circ as structural Verilog: 1 circuit, main circuit main
module main (
  input  [7:0] _1_letter,
  input  [7:0] _2_letter,
  input  [7:0] _3_letter,
  input  [7:0] _4_letter,
  input  [7:0] _5_letter,
  input  [7:0] _6_letter,
  input  [7:0] _7_letter,
  input  [7:0] _8_letter,
  input  start,
  input  clock,
  output [3:0] letterNumber
);

  wire main_1_lcount, main_1_reset;
  wire [3:0] main_1_sletter;

  LetterCounterControlUnit_main main_1 (
    .start(start), .clock(clock), .Sletter(main_1_sletter), .Reset(main_1_reset), .Lcount(main_1_lcount));
  LetterCounterDatapath_main main_2 (
    ._1_letter(_1_letter), ._2_letter(_2_letter), ._3_letter(_3_letter), ._4_letter(_4_letter),
    ._5_letter(_5_letter), ._6_letter(_6_letter), ._7_letter(_7_letter), ._8_letter(_8_letter),
    .Sletter(main_1_sletter), .Reset(main_1_reset), .Lcount(main_1_lcount), .clock(clock),
    .counter(letterNumber));
endmodule
