// Logisim project LetterCounterControlUnit.circ as structural Verilog: 1 circuit, main circuit main
module main (
  input  start,
  input  clock,
  output [3:0] Sletter,
  output Reset,
  output Lcount
);

  wire and_1_out, and_2_out, and_3_out, and_4_out, and_5_out, and_6_out, N3_out, not_1_out, not_2_out,
       not_3_out, not_4_out, not_5_out, not_6_out, not_7_out, not_8_out, not_9_out, not_10_out, not_11_out,
       not_12_out, not_13_out, not_14_out, not_15_out, not_16_out, not_17_out, not_18_out, not_19_out,
       or_1_out, xor_1_out, xor_2_out;
  wire [3:0] n0_out;

  Register #(.width(4)) STATE (.D(n0_out), .Q(Sletter), .clk(clock));  // open: en, clr
  xor xor_1 (xor_1_out, Sletter[2], Sletter[0]);
  not not_1 (not_1_out, Sletter[1]);
  and and_1 (and_1_out, not_1_out, start);
  not not_2 (not_2_out, Sletter[3]);
  and N3 (N3_out, not_2_out, Sletter[2], Sletter[1], Sletter[0]);
  not not_3 (not_3_out, Sletter[2]);
  and and_2 (and_2_out, Sletter[3], not_3_out, not_4_out, not_5_out);
  not not_4 (not_4_out, Sletter[1]);
  not not_5 (not_5_out, Sletter[0]);
  not not_6 (not_6_out, Sletter[3]);
  and and_3 (and_3_out, not_6_out, Sletter[1], xor_1_out);
  not not_7 (not_7_out, Sletter[3]);
  and and_4 (and_4_out, not_7_out, Sletter[2], not_8_out);
  not not_8 (not_8_out, Sletter[1]);
  xor xor_2 (xor_2_out, Sletter[1], Sletter[0]);
  not not_9 (not_9_out, Sletter[3]);
  not not_10 (not_10_out, Sletter[2]);
  and and_5 (and_5_out, not_9_out, not_10_out, not_11_out, or_1_out);
  not not_11 (not_11_out, Sletter[0]);
  or or_1 (or_1_out, and_1_out, Sletter[1]);
  not not_12 (not_12_out, Sletter[3]);
  and and_6 (and_6_out, not_12_out, Sletter[2], not_13_out);
  not not_13 (not_13_out, Sletter[0]);
  not not_14 (not_14_out, Sletter[2]);
  and and_7 (Lcount, Sletter[3], not_14_out, not_15_out, not_16_out);
  not not_15 (not_15_out, Sletter[1]);
  not not_16 (not_16_out, Sletter[0]);
  or n3_2 (n0_out[3], N3_out, and_2_out);
  or n2 (n0_out[2], and_3_out, and_4_out);
  not not_17 (not_17_out, Sletter[3]);
  and n1 (n0_out[1], not_17_out, xor_2_out);
  or n0 (n0_out[0], and_5_out, and_6_out, Lcount);
  not not_18 (not_18_out, Sletter[2]);
  and and_8 (Reset, Sletter[3], not_18_out, not_19_out, Sletter[0]);
  not not_19 (not_19_out, Sletter[1]);
endmodule
