// Logisim project LetterCounterDatapath.circ as structural Verilog: 1 circuit, main circuit main
module main (
  input  [7:0] _1_letter,
  input  [7:0] _2_letter,
  input  [7:0] _3_letter,
  input  [7:0] _4_letter,
  input  [7:0] _5_letter,
  input  [7:0] _6_letter,
  input  [7:0] _7_letter,
  input  [7:0] _8_letter,
  input  [3:0] Sletter,
  input  Reset,
  input  Lcount,
  input  clock,
  output [3:0] counter
);

  wire comparator_1_eq, not_1_out;
  wire [3:0] counter_1_q;
  wire [7:0] multiplexer_1_out;

  Multiplexer #(.select(4), .width(8), .enable("false")) multiplexer_1 (
    .in0(_1_letter), .in1(_2_letter), .in2(_3_letter), .in3(_4_letter), .in4(_5_letter), .in5(_6_letter),
    .in6(_7_letter), .in7(_8_letter), .in8({8{1'b0}}), .in9({8{1'b0}}), .out(multiplexer_1_out), .sel(Sletter));  // open: in10, in11, in12, in13, in14, in15
  not not_1 (not_1_out, comparator_1_eq);
  Comparator comparator_1 (.a({8{1'b0}}), .b(multiplexer_1_out), .eq(comparator_1_eq));  // open: gt, lt
  Counter #(.width(4), .max('h8)) counter_1 (
    .count(not_1_out), .Q(counter_1_q), .clk(clock), .clr(Reset));  // open: load, D, carry
  Register #(.width(4)) register_1 (.D(counter_1_q), .en(Lcount), .Q(counter), .clk(clock));  // open: clr
endmodule
