// Logisim project datapath.circ as structural Verilog: 1 circuit, main circuit main
module main (
  input  [7:0] _1_letter,
  input  L1,
  input  [7:0] _2_letter,
  input  L2,
  input  [7:0] _3_letter,
  input  L3,
  input  [7:0] _4_letter,
  input  L4,
  input  [7:0] _5_letter,
  input  L5,
  input  [7:0] _6_letter,
  input  L6,
  input  [7:0] _7_letter,
  input  L7,
  input  [7:0] _8_letter,
  input  L8,
  input  a,
  input  b,
  input  c,
  input  d,
  input  e,
  input  f,
  input  g,
  input  h,
  input  i,
  input  j,
  input  k,
  input  l,
  input  m,
  input  n,
  input  o,
  input  p,
  input  q,
  input  r,
  input  s,
  input  t,
  input  u,
  input  v,
  input  w,
  input  x,
  input  y,
  input  z,
  input  Reset,
  input  letter,
  input  comp,
  input  Rlet,
  input  Clock,
  input  Start,
  output [7:0] _1_letter_2,
  output [7:0] _2_letter_2,
  output [7:0] _3_letter_2,
  output [7:0] _4_letter_2,
  output [7:0] _5_letter_2,
  output [7:0] _6_letter_2,
  output [7:0] _7_letter_2,
  output [7:0] _8_letter_2,
  output win,
  output lose,
  output [3:0] counter
);

  wire _1_letter_2_q, _2_letter_2_q, _3_letter_2_q, _4_letter_2_q, _5_letter_2_q, _6_letter_2_q,
       _7_letter_2_q, _8_letter_2_q, comparator_1_eq, comparator_2_eq, comparator_3_eq, comparator_4_eq,
       comparator_5_eq, comparator_6_eq, comparator_7_eq, comparator_8_eq, multiplexer_2_out,
       multiplexer_3_out, multiplexer_4_out, multiplexer_5_out, multiplexer_6_out, multiplexer_7_out,
       multiplexer_8_out, multiplexer_9_out, not_1_out, or_1_out;
  wire [4:0] priority_encoder_1_out;
  wire [7:0] _1_letter_q, _2_letter_q, _3_letter_q, _4_letter_q, _5_letter_q, _6_letter_q, _7_letter_q,
       _8_letter_q, multiplexer_1_out, try_letter_q;

  Register u__1_letter (.D(_1_letter), .en(L1), .Q(_1_letter_q), .clk(Clock));  // open: clr
  Register u__2_letter (.D(_2_letter), .en(L2), .Q(_2_letter_q), .clk(Clock));  // open: clr
  Register u__3_letter (.D(_3_letter), .en(L3), .Q(_3_letter_q), .clk(Clock));  // open: clr
  Register u__4_letter (.D(_4_letter), .en(L4), .Q(_4_letter_q), .clk(Clock));  // open: clr
  Register u__5_letter (.D(_5_letter), .en(L5), .Q(_5_letter_q), .clk(Clock));  // open: clr
  Register u__6_letter (.D(_6_letter), .en(L6), .Q(_6_letter_q), .clk(Clock));  // open: clr
  Register u__7_letter (.D(_7_letter), .en(L7), .Q(_7_letter_q), .clk(Clock));  // open: clr
  Register u__8_letter (.D(_8_letter), .en(L8), .Q(_8_letter_q), .clk(Clock));  // open: clr
  Priority_Encoder #(.select(5)) priority_encoder_1 (
    .in0(a), .in1(b), .in2(c), .in3(d), .in4(e), .in5(f), .in6(g), .in7(h), .in8(i), .in9(j), .in10(k),
    .in11(l), .in12(m), .in13(n), .in14(o), .in15(p), .in16(q), .in17(r), .in18(s), .in19(t), .in20(u),
    .in21(v), .in22(w), .in23(x), .in24(y), .in25(z), .out(priority_encoder_1_out));  // open: in26, in27, in28, in29, in30, in31, gs, en_out, en_in
  Multiplexer #(.select(5), .width(8), .enable("false")) multiplexer_1 (
    .in0(8'h61), .in1(8'h62), .in2(8'h63), .in3(8'h64), .in4(8'h65), .in5(8'h66), .in6(8'h67), .in7(8'h68),
    .in8(8'h69), .in9(8'h6a), .in10(8'h6b), .in11(8'h6c), .in12(8'h6d), .in13(8'h6e), .in14(8'h6f),
    .in15(8'h70), .in16(8'h71), .in17(8'h72), .in18(8'h73), .in19(8'h74), .in20(8'h75), .in21(8'h76),
    .in22(8'h77), .in23(8'h78), .in24(8'h79), .in25(8'h7a), .out(multiplexer_1_out),
    .sel(priority_encoder_1_out));  // open: in26, in27, in28, in29, in30, in31
  Register try_letter (.D(multiplexer_1_out), .en(letter), .Q(try_letter_q), .clk(Clock), .clr(Rlet));
  Comparator comparator_1 (.a(_1_letter_q), .b(try_letter_q), .eq(comparator_1_eq));  // open: gt, lt
  Comparator comparator_2 (.a(_2_letter_q), .b(try_letter_q), .eq(comparator_2_eq));  // open: gt, lt
  Comparator comparator_3 (.a(_3_letter_q), .b(try_letter_q), .eq(comparator_3_eq));  // open: gt, lt
  Comparator comparator_4 (.a(_4_letter_q), .b(try_letter_q), .eq(comparator_4_eq));  // open: gt, lt
  Comparator comparator_5 (.a(_5_letter_q), .b(try_letter_q), .eq(comparator_5_eq));  // open: gt, lt
  Comparator comparator_6 (.a(_6_letter_q), .b(try_letter_q), .eq(comparator_6_eq));  // open: gt, lt
  Comparator comparator_7 (.a(_7_letter_q), .b(try_letter_q), .eq(comparator_7_eq));  // open: gt, lt
  Comparator comparator_8 (.a(_8_letter_q), .b(try_letter_q), .eq(comparator_8_eq));  // open: gt, lt
  Multiplexer #(.enable("false")) multiplexer_2 (
    .in0(1'b0), .in1(comparator_1_eq), .out(multiplexer_2_out), .sel(comp));
  Multiplexer #(.enable("false")) multiplexer_3 (
    .in0(1'b0), .in1(comparator_2_eq), .out(multiplexer_3_out), .sel(comp));
  Multiplexer #(.enable("false")) multiplexer_4 (
    .in0(1'b0), .in1(comparator_3_eq), .out(multiplexer_4_out), .sel(comp));
  Multiplexer #(.enable("false")) multiplexer_5 (
    .in0(1'b0), .in1(comparator_4_eq), .out(multiplexer_5_out), .sel(comp));
  Multiplexer #(.enable("false")) multiplexer_6 (
    .in0(1'b0), .in1(comparator_5_eq), .out(multiplexer_6_out), .sel(comp));
  Multiplexer #(.enable("false")) multiplexer_7 (
    .in0(1'b0), .in1(comparator_6_eq), .out(multiplexer_7_out), .sel(comp));
  Multiplexer #(.enable("false")) multiplexer_8 (
    .in0(1'b0), .in1(comparator_7_eq), .out(multiplexer_8_out), .sel(comp));
  Multiplexer #(.enable("false")) multiplexer_9 (
    .in0(1'b0), .in1(comparator_8_eq), .out(multiplexer_9_out), .sel(comp));
  or or_1 (or_1_out, comparator_1_eq, comparator_2_eq, comparator_3_eq, comparator_4_eq, comparator_5_eq, comparator_6_eq, comparator_7_eq, comparator_8_eq);
  Register #(.width(1)) u__1_letter_2 (.D(1'b1), .en(multiplexer_2_out), .Q(_1_letter_2_q), .clk(Clock), .clr(Start));
  Register #(.width(1)) u__2_letter_2 (.D(1'b1), .en(multiplexer_3_out), .Q(_2_letter_2_q), .clk(Clock), .clr(Start));
  Register #(.width(1)) u__3_letter_2 (.D(1'b1), .en(multiplexer_4_out), .Q(_3_letter_2_q), .clk(Clock), .clr(Start));
  Register #(.width(1)) u__4_letter_2 (.D(1'b1), .en(multiplexer_5_out), .Q(_4_letter_2_q), .clk(Clock), .clr(Start));
  Register #(.width(1)) u__5_letter_2 (.D(1'b1), .en(multiplexer_6_out), .Q(_5_letter_2_q), .clk(Clock), .clr(Start));
  Register #(.width(1)) u__6_letter_2 (.D(1'b1), .en(multiplexer_7_out), .Q(_6_letter_2_q), .clk(Clock), .clr(Start));
  Register #(.width(1)) u__7_letter_2 (.D(1'b1), .en(multiplexer_8_out), .Q(_7_letter_2_q), .clk(Clock), .clr(Start));
  Register #(.width(1)) u__8_letter_2 (.D(1'b1), .en(multiplexer_9_out), .Q(_8_letter_2_q), .clk(Clock), .clr(Start));
  Counter #(.width(4), .max('ha)) u_counter (
    .count(not_1_out), .Q(counter), .clk(Clock), .clr(Reset));  // open: load, D, carry
  not not_1 (not_1_out, or_1_out);
  Multiplexer #(.width(8), .enable("false")) multiplexer_10 (
    .in0(8'h2a), .in1(_1_letter_q), .out(_1_letter_2), .sel(_1_letter_2_q));
  Multiplexer #(.width(8), .enable("false")) multiplexer_11 (
    .in0(8'h2a), .in1(_2_letter_q), .out(_2_letter_2), .sel(_2_letter_2_q));
  Multiplexer #(.width(8), .enable("false")) multiplexer_12 (
    .in0(8'h2a), .in1(_3_letter_q), .out(_3_letter_2), .sel(_3_letter_2_q));
  Multiplexer #(.width(8), .enable("false")) multiplexer_13 (
    .in0(8'h2a), .in1(_4_letter_q), .out(_4_letter_2), .sel(_4_letter_2_q));
  Multiplexer #(.width(8), .enable("false")) multiplexer_14 (
    .in0(8'h2a), .in1(_5_letter_q), .out(_5_letter_2), .sel(_5_letter_2_q));
  Multiplexer #(.width(8), .enable("false")) multiplexer_15 (
    .in0(8'h2a), .in1(_6_letter_q), .out(_6_letter_2), .sel(_6_letter_2_q));
  Multiplexer #(.width(8), .enable("false")) multiplexer_16 (
    .in0(8'h2a), .in1(_7_letter_q), .out(_7_letter_2), .sel(_7_letter_2_q));
  Multiplexer #(.width(8), .enable("false")) multiplexer_17 (
    .in0(8'h2a), .in1(_8_letter_q), .out(_8_letter_2), .sel(_8_letter_2_q));
  Comparator #(.width(4)) comparator_9 (.a(4'b1010), .b(counter), .eq(lose));  // open: gt, lt
  and and_1 (win, _1_letter_2_q, _2_letter_2_q, _3_letter_2_q, _4_letter_2_q, _5_letter_2_q, _6_letter_2_q, _7_letter_2_q, _8_letter_2_q);

  // Notes on the sheet:
  //   first
  //   second
  //   third
  //   fourth
  //   fifth
  //   sixth
  //   seventh
  //   eighth
endmodule
