// Logisim project ledMatrix.circ as structural Verilog: 1 circuit, main circuit main
module main (
  input  [3:0] counter,
  output [6:0] c1,
  output [6:0] c2,
  output [6:0] c3,
  output [6:0] c4,
  output [6:0] c5
);

  Multiplexer #(.select(4), .width(7), .enable("false")) multiplexer_1 (
    .in0({7{1'b0}}), .in1({7{1'b1}}), .in2({7{1'b1}}), .in3({7{1'b1}}), .in4({7{1'b1}}), .in5({7{1'b1}}),
    .in6({7{1'b1}}), .in7({7{1'b1}}), .in8({7{1'b1}}), .in9({7{1'b1}}), .in10({7{1'b1}}), .out(c1),
    .sel(counter));  // open: in11, in12, in13, in14, in15
  Multiplexer #(.select(4), .width(7), .enable("false")) multiplexer_2 (
    .in0({7{1'b0}}), .in1({7{1'b0}}), .in2(7'b1000000), .in3(7'b1000000), .in4(7'b1000000), .in5(7'b1000000),
    .in6(7'b1000000), .in7(7'b1000000), .in8(7'b1000000), .in9(7'b1000000), .in10(7'b1000000), .out(c2),
    .sel(counter));  // open: in11, in12, in13, in14, in15
  Multiplexer #(.select(4), .width(7), .enable("false")) multiplexer_3 (
    .in0({7{1'b0}}), .in1({7{1'b0}}), .in2(7'b1000000), .in3(7'b1000000), .in4(7'b1000000), .in5(7'b1000000),
    .in6(7'b1000000), .in7(7'b1010000), .in8(7'b1010000), .in9(7'b1010100), .in10(7'b1010100), .out(c3),
    .sel(counter));  // open: in11, in12, in13, in14, in15
  Multiplexer #(.select(4), .width(7), .enable("false")) multiplexer_4 (
    .in0({7{1'b0}}), .in1({7{1'b0}}), .in2(7'b1000000), .in3(7'b1100000), .in4(7'b1110000), .in5(7'b1111000),
    .in6(7'b1111100), .in7(7'b1111100), .in8(7'b1111100), .in9(7'b1111100), .in10(7'b1111100), .out(c4),
    .sel(counter));  // open: in11, in12, in13, in14, in15
  Multiplexer #(.select(4), .width(7), .enable("false")) multiplexer_5 (
    .in0({7{1'b0}}), .in1({7{1'b0}}), .in2({7{1'b0}}), .in3({7{1'b0}}), .in4({7{1'b0}}), .in5({7{1'b0}}),
    .in6({7{1'b0}}), .in7({7{1'b0}}), .in8(7'b0010000), .in9(7'b0010000), .in10(7'b0010100), .out(c5),
    .sel(counter));  // open: in11, in12, in13, in14, in15
endmodule
