// Logisim project printTTY.circ as structural Verilog: 1 circuit, main circuit main
module main (
  input  [7:0] _1_letter,
  input  [7:0] _2_letter,
  input  [7:0] _3_letter,
  input  [7:0] _4_letter,
  input  [7:0] _5_letter,
  input  [7:0] _6_letter,
  input  [7:0] _7_letter,
  input  [7:0] _8_letter,
  input  reset,
  input  clk,
  output [6:0] print
);

  wire [3:0] counter_1_q;
  wire [7:0] multiplexer_1_out;

  Counter #(.width(4), .max('h8)) counter_1 (.Q(counter_1_q), .clk(clk), .clr(reset));  // open: load, D, count, carry
  Multiplexer #(.select(4), .width(8), .enable("false")) multiplexer_1 (
    .in0(_1_letter), .in1(_2_letter), .in2(_3_letter), .in3(_4_letter), .in4(_5_letter), .in5(_6_letter),
    .in6(_7_letter), .in7(_8_letter), .in8(8'hd), .out(multiplexer_1_out), .sel(counter_1_q));  // open: in9, in10, in11, in12, in13, in14, in15
  Bit_Extender #(.out_width(7), .\type ("one")) bit_extender_1 (.in(multiplexer_1_out), .out(print));
endmodule
