// Logisim project scoreBoard.circ as structural Verilog: 1 circuit, main circuit main
module main (
  input  win,
  input  Reset,
  input  lose,
  output [3:0] player,
  output [3:0] computer
);

  Counter #(.width(4), .max('hf)) counter_1 (.Q(player), .clk(win), .clr(Reset));  // open: load, D, count, carry
  Counter #(.width(4), .max('hf)) counter_2 (.Q(computer), .clk(lose), .clr(Reset));  // open: load, D, count, carry
endmodule
