// Logisim project ButtonPressSynchronizer.circ as structural Verilog: 1 circuit, main circuit main
module main (
  input  B,
  input  clock,
  output b_2
);

  wire not_1_out, not_2_out, not_3_out, xor_1_out;
  wire [1:0] and_3_out, STATE_q;

  Register #(.width(2)) STATE (.D(and_3_out), .en(1'b1), .Q(STATE_q), .clk(clock));  // open: clr
  xor xor_1 (xor_1_out, STATE_q[1], STATE_q[0]);
  not not_1 (not_1_out, STATE_q[1]);
  not not_2 (not_2_out, STATE_q[1]);
  not not_3 (not_3_out, STATE_q[0]);
  and and_1 (b_2, not_1_out, STATE_q[0]);
  and and_2 (and_3_out[1], B, xor_1_out);
  and and_3 (and_3_out[0], B, not_2_out, not_3_out);

  // Notes on the sheet:
  //   s0
  //   s1
  //   n1
  //   n0
endmodule
