// Logisim project ControlUnit.circ as structural Verilog: 1 circuit, main circuit main
module main (
  input  B1,
  input  B2,
  input  R,
  input  clock,
  output P1,
  output P2,
  output led1,
  output led2,
  output led3,
  output led4,
  output led5,
  output led6,
  output led7
);

  wire and_1_out, and_2_out, and_3_out, and_4_out, and_5_out, and_6_out, and_7_out, and_8_out, and_11_out,
       and_12_out, and_13_out, and_14_out, and_15_out, and_16_out, and_17_out, and_18_out, and_19_out,
       and_20_out, and_21_out, not_1_out, not_2_out, not_3_out, not_4_out, not_5_out, not_6_out, not_7_out,
       not_8_out, not_9_out, not_10_out, not_11_out, not_12_out, not_13_out, not_14_out, not_15_out,
       not_16_out, not_17_out, not_18_out, not_19_out, not_20_out, not_21_out, not_22_out, not_23_out,
       not_24_out, not_25_out, not_26_out, or_1_out, or_2_out, or_3_out, or_4_out, or_5_out, or_6_out,
       or_7_out, R_prime_out, xor_1_out, xor_2_out, xor_3_out;
  wire [2:0] or_9_out, STATE_q;

  not R_prime (R_prime_out, R);
  not not_1 (not_1_out, B1);
  not not_2 (not_2_out, B2);
  not not_3 (not_3_out, B1);
  not not_4 (not_4_out, B2);
  not not_5 (not_5_out, B1);
  not not_6 (not_6_out, B2);
  not not_7 (not_7_out, STATE_q[2]);
  not not_8 (not_8_out, STATE_q[1]);
  not not_9 (not_9_out, STATE_q[2]);
  not not_10 (not_10_out, B1);
  not not_11 (not_11_out, B2);
  Register #(.width(3)) STATE (.D(or_9_out), .en(1'b1), .Q(STATE_q), .clk(clock));  // open: clr
  xor xor_1 (xor_1_out, STATE_q[1], STATE_q[0]);
  and and_1 (and_1_out, not_1_out, not_2_out);
  and and_2 (and_2_out, not_3_out, not_4_out);
  and and_3 (and_3_out, not_5_out, not_6_out);
  and and_4 (and_4_out, not_7_out, not_8_out);
  and and_5 (and_5_out, STATE_q[2], STATE_q[1]);
  xor xor_2 (xor_2_out, B1, B2);
  and and_6 (and_6_out, not_9_out, STATE_q[1]);
  and and_7 (and_7_out, B1, B2);
  and and_8 (and_8_out, not_10_out, not_11_out);
  xor xor_3 (xor_3_out, STATE_q[2], STATE_q[1]);
  not not_12 (not_12_out, STATE_q[2]);
  not not_13 (not_13_out, STATE_q[1]);
  not not_14 (not_14_out, STATE_q[2]);
  not not_15 (not_15_out, STATE_q[2]);
  or or_1 (or_1_out, B1, and_1_out);
  not not_16 (not_16_out, B2);
  not not_17 (not_17_out, STATE_q[1]);
  not not_18 (not_18_out, STATE_q[0]);
  or or_2 (or_2_out, B2, and_2_out);
  or or_3 (or_3_out, B1, and_3_out);
  or or_4 (or_4_out, and_4_out, and_5_out);
  or or_5 (or_5_out, STATE_q[2], and_6_out);
  or or_6 (or_6_out, and_7_out, and_8_out);
  and and_9 (P1, not_12_out, not_13_out, STATE_q[0]);
  and and_10 (P2, STATE_q[2], STATE_q[1], STATE_q[0]);
  and and_11 (and_11_out, R_prime_out, not_14_out, xor_1_out);
  and and_12 (and_12_out, R_prime_out, or_1_out, not_15_out, STATE_q[1], STATE_q[0]);
  and and_13 (and_13_out, R_prime_out, B1, not_16_out, STATE_q[2], not_17_out, not_18_out);
  not not_19 (not_19_out, STATE_q[0]);
  not not_20 (not_20_out, STATE_q[2]);
  not not_21 (not_21_out, B2);
  not not_22 (not_22_out, STATE_q[1]);
  not not_23 (not_23_out, STATE_q[0]);
  not not_24 (not_24_out, B1);
  not not_25 (not_25_out, STATE_q[1]);
  and and_14 (and_14_out, R_prime_out, or_2_out, STATE_q[1], not_19_out);
  and and_15 (and_15_out, R_prime_out, or_3_out, not_20_out, STATE_q[1], STATE_q[0]);
  and and_16 (and_16_out, R_prime_out, B1, not_21_out, STATE_q[2], not_22_out, not_23_out);
  and and_17 (and_17_out, R_prime_out, not_24_out, B2, STATE_q[2], not_25_out, STATE_q[0]);
  and and_18 (and_18_out, R_prime_out, STATE_q[2], STATE_q[1], STATE_q[0]);
  not not_26 (not_26_out, STATE_q[0]);
  or or_7 (or_7_out, and_11_out, and_12_out, and_13_out);
  and and_19 (and_19_out, R_prime_out, STATE_q[0], or_4_out);
  and and_20 (and_20_out, R_prime_out, xor_2_out, not_26_out, or_5_out);
  and and_21 (and_21_out, R_prime_out, or_6_out, STATE_q[0], xor_3_out);
  not n2 (or_9_out[2], or_7_out);
  or or_8 (or_9_out[1], and_14_out, and_15_out, and_16_out, and_17_out, and_18_out);
  or or_9 (or_9_out[0], and_19_out, and_20_out, and_21_out);
  Decoder #(.select(3)) decoder_1 (
    .out1(led1), .out2(led2), .out3(led3), .out4(led4), .out5(led5), .out6(led6), .out7(led7), .sel(STATE_q),
    .en(1'b1));  // open: out0

  // Notes on the sheet:
  //   l1
  //   l2
  //   s2
  //   s0
  //   s1
  //   l0
  //   n2'
  //   n1
  //   n0
endmodule
