// Logisim project Datapath.circ as structural Verilog: 1 circuit, main circuit main
module main (
  input  P1,
  input  Rscore,
  input  P2,
  output [3:0] P1score,
  output [3:0] P2score
);

  Counter #(.width(4), .max('hf)) counter_1 (.Q(P1score), .clk(P1), .clr(Rscore));  // open: load, D, count, carry
  Counter #(.width(4), .max('hf)) counter_2 (.Q(P2score), .clk(P2), .clr(Rscore));  // open: load, D, count, carry
endmodule
