// Logisim project Decoder.circ as structural Verilog: 1 circuit, main circuit main
module main (
  input  [3:0] number,
  output a,
  output b,
  output c,
  output d,
  output e,
  output f,
  output g
);

  wire and_1_out, and_2_out, and_3_out, and_4_out, and_5_out, and_6_out, and_7_out, and_8_out, and_9_out,
       and_10_out, and_11_out, n0_out, n1_out, n2_out, n3_out, or_1_out, or_3_out, or_4_out, xnor_1_out,
       xor_1_out, xor_2_out, xor_3_out, xor_4_out, xor_5_out;

  not n0 (n0_out, number[0]);
  not n1 (n1_out, number[1]);
  not n2 (n2_out, number[2]);
  not n3 (n3_out, number[3]);
  xor xor_1 (xor_1_out, number[0], number[2]);
  xor xor_2 (xor_2_out, number[1], number[0]);
  xor xor_3 (xor_3_out, number[2], number[0]);
  xnor xnor_1 (xnor_1_out, number[2], number[1]);
  xor xor_4 (xor_4_out, number[3], number[1]);
  xor xor_5 (xor_5_out, number[1], number[0]);
  and and_1 (and_1_out, n1_out, n3_out, xor_1_out);
  and and_2 (and_2_out, n3_out, number[2], xor_2_out);
  and and_3 (and_3_out, n3_out, n2_out, number[1], n0_out);
  and and_4 (and_4_out, n3_out, n1_out, xor_3_out);
  and and_5 (and_5_out, n3_out, number[2], number[1], number[0]);
  and and_6 (and_6_out, n3_out, n0_out, xnor_1_out);
  and and_7 (and_7_out, n2_out, n0_out, xor_4_out);
  and and_8 (and_8_out, n3_out, n2_out, xor_5_out);
  and and_9 (and_9_out, n3_out, number[1], number[0]);
  and and_10 (and_10_out, n3_out, n2_out, n1_out);
  and and_11 (and_11_out, n3_out, number[2], number[1], number[0]);
  not not_1 (a, and_1_out);
  not not_2 (b, and_2_out);
  not not_3 (c, and_3_out);
  not not_4 (d, or_1_out);
  or or_1 (or_1_out, and_4_out, and_5_out);
  or or_2 (e, and_6_out, and_7_out);
  not not_5 (f, or_3_out);
  or or_3 (or_3_out, and_8_out, and_9_out);
  not not_6 (g, or_4_out);
  or or_4 (or_4_out, and_10_out, and_11_out);
endmodule
