// Logisim project TheGame.circ as structural Verilog: 1 circuit, main circuit main
module main (
  input  in_1,
  input  led1
);

  wire B1_out, B2_out, clk_out, main_1_b_2, main_2_b_2, main_3_led1, main_3_led2, main_3_led3, main_3_led4,
       main_3_led5, main_3_led6, main_3_led7, main_3_p1, main_3_p2, main_5_a, main_5_b, main_5_c, main_5_d,
       main_5_e, main_5_f, main_5_g, main_6_a, main_6_b, main_6_c, main_6_d, main_6_e, main_6_f, main_6_g,
       R_out, Rscore_out;
  wire [3:0] main_4_p1score, main_4_p2score;

  Button Rscore (.out(Rscore_out));
  Button B1 (.out(B1_out));
  Button B2 (.out(B2_out));
  Button R (.out(R_out));
  Clock clk (.out(clk_out));
  ButtonPressSynchronizer_main main_1 (.B(B1_out), .clock(clk_out), .b_2(main_1_b_2));
  ButtonPressSynchronizer_main main_2 (.B(B2_out), .clock(clk_out), .b_2(main_2_b_2));
  ControlUnit_main main_3 (
    .B1(main_1_b_2), .B2(main_2_b_2), .R(R_out), .clock(clk_out), .P1(main_3_p1), .P2(main_3_p2),
    .led1(main_3_led1), .led2(main_3_led2), .led3(main_3_led3), .led4(main_3_led4), .led5(main_3_led5),
    .led6(main_3_led6), .led7(main_3_led7));
  Datapath_main main_4 (
    .P1(main_3_p1), .Rscore(Rscore_out), .P2(main_3_p2), .P1score(main_4_p1score), .P2score(main_4_p2score));
  Decoder_main main_5 (
    .number(main_4_p1score), .a(main_5_a), .b(main_5_b), .c(main_5_c), .d(main_5_d), .e(main_5_e),
    .f(main_5_f), .g(main_5_g));
  Decoder_main main_6 (
    .number(main_4_p2score), .a(main_6_a), .b(main_6_b), .c(main_6_c), .d(main_6_d), .e(main_6_e),
    .f(main_6_f), .g(main_6_g));
  LED led_1 (.in(main_3_led1));
  LED led_2 (.in(main_3_led2));
  LED led_3 (.in(main_3_led3));
  LED led_4 (.in(main_3_led4));
  LED led_5 (.in(main_3_led5));
  LED led_6 (.in(main_3_led6));
  LED led_7 (.in(main_3_led7));
  _7_Segment_Display u_7_segment_display_1 (
    .g(main_5_g), .f(main_5_f), .a(main_5_a), .b(main_5_b), .e(main_5_e), .d(main_5_d), .c(main_5_c),
    .dp(in_1));
  _7_Segment_Display u_7_segment_display_2 (
    .g(main_6_g), .f(main_6_f), .a(main_6_a), .b(main_6_b), .e(main_6_e), .d(main_6_d), .c(main_6_c),
    .dp(led1));

  // Notes on the sheet:
  //   Button Press Sychronizer
  //   Button Press Sychronizer
  //   datapath for ScoreBoard
  //   Decoder
  //   Decoder
  //   led2
  //   led3
  //   led4
  //   led5
  //   led6
  //   led7
  //   Player1 Score
  //   Player2 Score
endmodule
