// Logisim project ControlUnit.circ as structural Verilog: 1 circuit, main circuit main
module main (
  input  NotGt,
  input  Gt,
  input  Start,
  input  Clk,
  output Sa,
  output La,
  output Lb,
  output Smult,
  output Lmult,
  output Sadd
);

  wire and_1_out, and_2_out, and_3_out, and_4_out, and_5_out, not_1_out, not_2_out, not_3_out, not_4_out,
       not_5_out, not_6_out, not_7_out, not_8_out, not_9_out, not_10_out, not_11_out, not_12_out, not_13_out,
       not_14_out, not_15_out, not_16_out, not_17_out, or_1_out, or_2_out, or_3_out, xor_1_out, xor_2_out;
  wire [2:0] and_13_out, STATE_q;

  Register #(.width(3)) STATE (.D(and_13_out), .en(1'b1), .Q(STATE_q), .clk(Clk));  // open: clr
  xor xor_1 (xor_1_out, STATE_q[2], STATE_q[0]);
  not not_1 (not_1_out, STATE_q[0]);
  and and_1 (and_1_out, not_1_out, NotGt);
  xor xor_2 (xor_2_out, STATE_q[2], STATE_q[0]);
  not not_2 (not_2_out, STATE_q[1]);
  and and_2 (and_2_out, not_2_out, Start);
  or or_1 (or_1_out, NotGt, Gt);
  or or_2 (or_2_out, and_1_out, STATE_q[0]);
  not not_3 (not_3_out, STATE_q[1]);
  and and_3 (and_3_out, not_3_out, xor_2_out);
  not not_4 (not_4_out, STATE_q[2]);
  and and_4 (and_4_out, not_4_out, STATE_q[1], not_5_out, Gt);
  not not_5 (not_5_out, STATE_q[0]);
  and and_5 (and_5_out, STATE_q[1], or_1_out);
  and and_6 (Sa, STATE_q[2], not_6_out, not_7_out);
  not not_6 (not_6_out, STATE_q[1]);
  not not_7 (not_7_out, STATE_q[0]);
  not not_8 (not_8_out, STATE_q[1]);
  and and_7 (La, not_8_out, xor_1_out);
  not not_9 (not_9_out, STATE_q[2]);
  and and_8 (Lb, not_9_out, not_10_out, STATE_q[0]);
  not not_10 (not_10_out, STATE_q[1]);
  not not_11 (not_11_out, STATE_q[2]);
  and and_9 (Smult, not_11_out, STATE_q[1], STATE_q[0]);
  not not_12 (not_12_out, STATE_q[2]);
  and and_10 (Lmult, not_12_out, STATE_q[0]);
  and and_11 (Sadd, STATE_q[2], not_13_out, not_14_out);
  not not_13 (not_13_out, STATE_q[1]);
  not not_14 (not_14_out, STATE_q[0]);
  not not_15 (not_15_out, STATE_q[2]);
  not not_16 (not_16_out, STATE_q[2]);
  not not_17 (not_17_out, STATE_q[0]);
  or or_3 (or_3_out, and_2_out, and_5_out);
  and and_12 (and_13_out[2], not_15_out, STATE_q[1], or_2_out);
  or or_4 (and_13_out[1], and_3_out, and_4_out);
  and and_13 (and_13_out[0], not_16_out, not_17_out, or_3_out);

  // Notes on the sheet:
  //   P1
  //   P2
  //   P0
  //   N2
  //   N1
  //   N0
endmodule
