// Logisim project Project2.circ as structural Verilog: 1 circuit, main circuit main
module main (
  input  [15:0] a,
  input  [15:0] b,
  output [15:0] Result
);

  wire Clk_out, main_1_la, main_1_lb, main_1_lmult, main_1_sa, main_1_sadd, main_1_smult, main_2_gt,
       main_2_notgt, Start_out;

  Button Start (.out(Start_out));
  Clock Clk (.out(Clk_out));
  ControlUnit_main main_1 (
    .NotGt(main_2_notgt), .Gt(main_2_gt), .Start(Start_out), .Clk(Clk_out), .Sa(main_1_sa), .La(main_1_la),
    .Lb(main_1_lb), .Smult(main_1_smult), .Lmult(main_1_lmult), .Sadd(main_1_sadd));
  datapath_main main_2 (
    .Sa(main_1_sa), .a_i(a), .La(main_1_la), .b_i(b), .Lb(main_1_lb), .Smult(main_1_smult),
    .Lmult(main_1_lmult), .Sadd(main_1_sadd), .Clk(Clk_out), .Gt(main_2_gt), .NotGt(main_2_notgt),
    .Result(Result));
endmodule
