// Logisim project datapath.circ as structural Verilog: 1 circuit, main circuit main
module main (
  input  Sa,
  input  [15:0] a_i,
  input  La,
  input  [15:0] b_i,
  input  Lb,
  input  Smult,
  input  Lmult,
  input  Sadd,
  input  Clk,
  output Gt,
  output NotGt,
  output [15:0] Result
);

  wire comparator_1_eq, comparator_1_lt;
  wire [15:0] a_q, adder_1_out, b_q, demultiplexer_1_out0, demultiplexer_1_out1, multiplexer_1_out,
       multiplexer_2_out, multiplexer_3_out, multiplexer_4_out;

  Multiplexer #(.width(16), .enable("false")) multiplexer_1 (
    .in0(a_i), .in1(demultiplexer_1_out1), .out(multiplexer_1_out), .sel(Sa));
  Multiplexer #(.width(16), .enable("false")) multiplexer_2 (
    .in0({16{1'b0}}), .in1(demultiplexer_1_out0), .out(multiplexer_2_out), .sel(Smult));
  Register #(.width(16)) a (.D(multiplexer_1_out), .en(La), .Q(a_q), .clk(Clk));  // open: clr
  Register #(.width(16)) b (.D(b_i), .en(Lb), .Q(b_q), .clk(Clk));  // open: clr
  Register #(.width(16)) mult (.D(multiplexer_2_out), .en(Lmult), .Q(Result), .clk(Clk));  // open: clr
  Comparator #(.width(16)) comparator_1 (.a(a_q), .b({16{1'b0}}), .gt(Gt), .eq(comparator_1_eq), .lt(comparator_1_lt));
  Multiplexer #(.width(16), .enable("false")) multiplexer_3 (
    .in0(Result), .in1(a_q), .out(multiplexer_3_out), .sel(Sadd));
  Multiplexer #(.width(16), .enable("false")) multiplexer_4 (
    .in0(b_q), .in1({16{1'b1}}), .out(multiplexer_4_out), .sel(Sadd));
  or \or  (NotGt, comparator_1_eq, comparator_1_lt);
  Adder #(.width(16)) adder_1 (
    .a(multiplexer_3_out), .b(multiplexer_4_out), .out(adder_1_out), .cin(1'b0));  // open: cout
  Demultiplexer #(.width(16), .enable("false")) demultiplexer_1 (
    .out0(demultiplexer_1_out0), .out1(demultiplexer_1_out1), .in(adder_1_out), .sel(Sadd));

  // Notes on the sheet:
  //   a - 1
  //   mult + b
  //   mult
  //   a
  //   b
  //   -1
  //   mult + b
  //   a - 1
  //   mult
endmodule
